# Fritzing sketch Audio Transceiver(Part2) (saved by Fritzing 0.9.3b)
circuit board: 4.99999cm x 4.99999cm
breadboards: 1

parts:
  LM386 = LM386 [package=dip08]
  VCC2 = Battery block 9V
  10k_Pot = Trimmer Potentiometer [maximum_resistance=10kΩ package=THT]
  10K = Resistor [tolerance=±5% resistance=10k package=THT]
  0_1uF = Ceramic Capacitor [capacitance=0.1µF package="100 mil [THT, multilayer]"]
  10uF = Electrolytic Capacitor [capacitance=1µF package="100 mil [THT, electrolytic]"]
  220uF = Ceramic Capacitor [capacitance=0.22mF package="100 mil [THT, multilayer]"]
  LDR = Photocell (LDR) [package=THT]
  G_SPK = female pin header, 2 pins [form="♀ (female)"]
  G_Laser = female pin header, 2 pins [form="♀ (female)"]
  LM386_2 = LM386 [package=dip08]
  VCC3 = Battery block 9V
  10K_2 = Resistor [tolerance=±5% resistance=10k package=THT]
  0_1uF_2 = Ceramic Capacitor [capacitance=0.1µF package="100 mil [THT, multilayer]"]
  10uF_2 = Electrolytic Capacitor [capacitance=10µF package="100 mil [THT, electrolytic]"]
  G_Aux = female pin header, 2 pins [form="♀ (female)"]
  10K_pot = Trimmer Potentiometer [maximum_resistance=10kΩ package=THT]

nets:
  N1: LM386.GAIN, 10uF.-, 10uF.+
  N2: LM386.-IN, LM386.V-, VCC2.-, 10k_Pot.wiper, LDR.pin_0, G_SPK.pin2
  N3: LM386.+IN, 0_1uF.0
  N4: LM386.OUT, 220uF.1
  N5: LM386.V+, VCC2.+, 10k_Pot.leg1
  N6: 10k_Pot.leg2, 10K.Pin_1
  N7: 10K.Pin_0, 0_1uF.1, LDR.pin_1
  N8: 220uF.0, G_SPK.pin1
  N9: G_Laser.pin1, LM386_2.-IN, LM386_2.V-, VCC3.-, G_Aux.pin2, 10K_pot.wiper
  N10: G_Laser.pin2, LM386_2.OUT
  N11: LM386_2.GAIN, 10uF_2.-, 10uF_2.+
  N12: LM386_2.+IN, 0_1uF_2.0
  N13: LM386_2.V+, VCC3.+, 10K_pot.leg1
  N14: 10K_2.Pin_0, 0_1uF_2.1, G_Aux.pin1
  N15: 10K_2.Pin_1, 10K_pot.leg2

notes:
  G
  V
