# Fritzing sketch Audio Transceiver (saved by Fritzing 0.9.3b)
circuit board: 3.42785cm x 3.36705cm
breadboards: 1

parts:
  U1 = LM386 [package=dip08]
  C1 = Electrolytic Capacitor [capacitance=10µF package="200 mil [THT, electrolytic]"]
  VCC1 = Battery block 9V
  R2 = Resistor [tolerance=±5% resistance=10k package=THT]
  C3 = Ceramic Capacitor [capacitance=0.1µF package="100 mil [THT, multilayer]"]
  R1 = Trimmer Potentiometer [maximum_resistance=10kΩ package=THT]
  U2 = 2.5mm Audio Jack [package=stereojack2.5mm_stereojack2.5mm]
  J2 = female pin header, 2 pins [form="♀ (female)"]

nets:
  N1: U1.GAIN, C1.-, C1.+
  N2: U1.-IN, U1.V-, VCC1.-, R1.leg1, U2.RIGHT, J2.pin1
  N3: U1.+IN, C3.0
  N4: U1.OUT, J2.pin2
  N5: U1.V+, VCC1.+, R1.wiper
  N6: R2.Pin_0, C3.1, U2.SLEEVE
  N7: R2.Pin_1, R1.leg2
